# Fritzing sketch MCU principal (saved by Fritzing 0.9.3b)
breadboards: 1

parts:
  U1 = ESP32-38PinWide [part_number=ESP32-38PinWide]
  부품2 = FC-28 Soil Hygrometer Module - Probe
  부품3 = FC-28 Soil Hygrometer Module
  부품4 = FC-28 Soil Hygrometer Module
  부품5 = FC-28 Soil Hygrometer Module
  부품6 = FC-28 Soil Hygrometer Module - Probe
  부품7 = FC-28 Soil Hygrometer Module - Probe
  KF-1 = KF-301 Relay [package=THT]
  DHT1 = Humidity and Temperature Sensor DHT11  # not connected
  BULB1 = Incandescent light bulb small [package="bulb sm"]

nets:
  VCC: U1.VIN, 부품3.VCC, 부품4.VCC, 부품5.VCC
  GND: U1.GND, 부품3.GND, 부품4.GND, 부품5.GND
  N1: 부품2.POS, 부품3.POS
  N2: 부품2.NEG, 부품3.NEG
  N3: 부품4.POS, 부품6.POS
  N4: 부품4.NEG, 부품6.NEG
  N5: 부품5.POS, 부품7.POS
  N6: 부품5.NEG, 부품7.NEG
  N7: KF-1.C, BULB1.1

custom parts:
  ESP32-38PinWide: Generic 38-Pin ESP32 with wide format (only access to one side of pins on a breadboard) based on Stephen Lilley's HiLetgo ESP-WROOM-32 ESP32 ESP-32S Development Board.
  FC-28 Soil Hygrometer Module - Probe: The FC-28 is a soil hygrometer module that uses the Texas Instruments LM393 comparator chip to provide an analog measurement of soil humidity.
  FC-28 Soil Hygrometer Module: The FC-28 is a soil hygrometer module that uses the Texas Instruments LM393 comparator chip to provide an analog measurement of soil humidity. The digital output is high when soil moisture is over a certain threshold, as determined by adjusting the potentiometer.
  KF-301 Relay: KF-301
  Humidity and Temperature Sensor DHT11: Digital relative humidity & temperature sensor DHT11
